# Fritzing sketch buttons_menu (saved by Fritzing 0.9.3b)
breadboards: 1

parts:
  LCD1 = LCD screen
  R2 = Resistor [tolerance=±5% resistance=220 package=THT]
  Part1 = Arduino Uno (Rev3)
  R1 = Rotary Potentiometer (Small) [maximum_resistance=10kΩ package=THT]
  S1 = Pushbutton [package="[THT]"]
  S2 = Pushbutton [package="[THT]"]
  S4 = Pushbutton [package="[THT]"]
  S5 = Pushbutton [package="[THT]"]
  R3 = Resistor [tolerance=±5% resistance=220 package=THT]
  LED1 = LED - 5mm [color="Red (633nm)" package="5 mm [THT]"]
  S3 = Pushbutton [package="[THT]"]
  T1 = LM35 Temperature Sensor [package="TO92 [THT]"]
  R4 = Resistor [tolerance=±5% resistance=220 package=THT]
  LED2 = LED - 5mm [color="Red (633nm)" package="5 mm [THT]"]

nets:
  GND: LCD1.VSS, LCD1.R/W, LCD1.LED-, Part1.GND, R1.leg2, S1.Pin_3, S1.Pin_4, S2.Pin_3, S2.Pin_4, S4.Pin_3, S4.Pin_4, S5.Pin_3, S5.Pin_4, LED1.cathode, S3.Pin_3, S3.Pin_4, T1.GND, LED2.cathode
  VDD: LCD1.VDD, R2.Pin_0, Part1.5V, R1.leg1, T1.+Vs
  N1: LCD1.V0, R1.wiper
  N2: LCD1.RS, Part1.D12/MISO
  N3: LCD1.E, Part1.D11_PWM/MOSI
  N4: LCD1.DB4, Part1.D5_PWM
  N5: LCD1.DB5, Part1.D4
  N6: LCD1.DB6, Part1.D3_PWM
  N7: LCD1.DB7, Part1.D2
  N8: LCD1.LED+, R2.Pin_1
  left: Part1.A0, S1.Pin_1, S1.Pin_2
  N9: Part1.A5/SCL, T1.Vout
  N10: Part1.D8, S5.Pin_1, S5.Pin_2
  up: Part1.D9_PWM, S3.Pin_1, S3.Pin_2
  enter: Part1.D10_PWM/SS, S2.Pin_1, S2.Pin_2
  N11: Part1.D13/SCK, R4.Pin_1
  LED: Part1.D6_PWM, R3.Pin_1
  down/right: Part1.D7, S4.Pin_1, S4.Pin_2
  N12: R3.Pin_0, LED1.anode
  N13: R4.Pin_0, LED2.anode

notes:
  Left
  Right
  Enter
  Down
  Up
