# Fritzing sketch I2C_menu (saved by Fritzing 0.9.3b)

parts:
  LCD1 = LCD screen  # not connected
  Part1 = Arduino Uno (Rev3)
  J2 = male pin header, 4 pins [form="♂ (male)"]

nets:
  N1: Part1.A4/SDA, J2.pin3
  N2: Part1.A5/SCL, J2.pin4
  N3: Part1.5V, J2.pin2
  N4: Part1.GND, J2.pin1
