# Fritzing sketch hello_menu (saved by Fritzing 0.9.3b)
breadboards: 1

parts:
  LCD1 = LCD screen
  R2 = Resistor [tolerance=±5% resistance=220 package=THT]
  Part1 = Arduino Uno (Rev3)
  R1 = Rotary Potentiometer (Small) [maximum_resistance=10kΩ package=THT]
  R3 = Trimmer Potentiometer [maximum_resistance=10kΩ package=THT]
  R4 = Trimmer Potentiometer [maximum_resistance=10kΩ package=THT]

nets:
  VSS: LCD1.VSS, LCD1.R/W, LCD1.LED-, Part1.GND, R1.leg2, R3.leg2, R4.leg2
  VDD: LCD1.VDD, R2.Pin_0, Part1.5V, R1.leg1, R3.leg1, R4.leg1
  N1: LCD1.V0, R1.wiper
  N2: LCD1.RS, Part1.D12/MISO
  N3: LCD1.E, Part1.D11_PWM/MOSI
  N4: LCD1.DB4, Part1.D5_PWM
  N5: LCD1.DB5, Part1.D4
  N6: LCD1.DB6, Part1.D3_PWM
  N7: LCD1.DB7, Part1.D2
  N8: LCD1.LED+, R2.Pin_1
  N9: Part1.A1, R3.wiper
  N10: Part1.A2, R4.wiper
